# Fritzing sketch stepping_motor_m35sp-7 (saved by Fritzing 0.9.4)
breadboards: 1

parts:
  LLC1 = LLC_4_X_5_3
  S1 = Ponte-H L298N
  Raspberry_Pi_1 = Raspberry Pi 3 [part_number=RPI-3-V1.2]
  J1 = T Cobbler Plus
  MOTOR4 = 28BYJ-48 Stepper Motor
  Part1 = Variable Capacitor [capacitance=100nF max_capacitance=10pF min_capacitance=2pF voltage=35V]
  Part2 = Variable Capacitor [capacitance=100nF max_capacitance=10pF min_capacitance=2pF voltage=35V]

nets:
  N1: LLC1.connector0, J1.#23
  N2: LLC1.connector1, J1.#22
  N3: LLC1.connector2, J1.3V3
  N4: LLC1.connector3, J1.GND#8
  N5: LLC1.connector4, J1.#27
  N6: LLC1.connector5, J1.#17
  N7: LLC1.connector6, S1.connector8
  N8: LLC1.connector7, S1.connector7
  N9: LLC1.connector9, S1.connector2, J1.GND#5, Part2.1
  N10: LLC1.connector10, J1.5.0V#3
  N11: LLC1.connector11, S1.connector6
  N12: LLC1.connector12, S1.connector5
  N13: S1.connector1, Part1.1
  N14: S1.connector10, MOTOR4.PINK
  N15: S1.connector11, MOTOR4.BLUE
  N16: S1.connector13, MOTOR4.ORANGE
  N17: S1.connector14, MOTOR4.RED
  3V3: Raspberry_Pi_1.3v3, Raspberry_Pi_1.3V3, J1.3.3V#41, J1.3.3V#57
  N18: Raspberry_Pi_1.GPIO2, J1.GPIO_2
  N19: Raspberry_Pi_1.GPIO3, J1.GPIO_3
  N20: Raspberry_Pi_1.GPIO4, J1.GPIO_4
  N21: Raspberry_Pi_1.GND, J1.GND#46, J1.GND#49, J1.GND#54, J1.GND#60, J1.GND#65, J1.GND#70, J1.GND#74, J1.GND#79
  N22: Raspberry_Pi_1.GPIO17, J1.GPIO_17
  N23: Raspberry_Pi_1.GPIO27, J1.GPIO_27
  N24: Raspberry_Pi_1.GPIO22, J1.GPIO_22
  N25: Raspberry_Pi_1.GPIO10, J1.GPIO_10
  N26: Raspberry_Pi_1.GPIO9, J1.GPIO_9
  N27: Raspberry_Pi_1.GPIO11, J1.GPIO_11
  N28: Raspberry_Pi_1.ID_SD, J1.ID_SD
  N29: Raspberry_Pi_1.GPIO5, J1.GPIO_5
  N30: Raspberry_Pi_1.GPIO6, J1.GPIO_6
  N31: Raspberry_Pi_1.GPIO13, J1.GPIO_13
  N32: Raspberry_Pi_1.GPIO19, J1.GPIO_19
  N33: Raspberry_Pi_1.GPIO26, J1.GPIO_26
  N34: Raspberry_Pi_1.GPIO21, J1.GPIO_21
  N35: Raspberry_Pi_1.GPIO20, J1.GPIO_20
  N36: Raspberry_Pi_1.GPIO16, J1.GPIO_16
  N37: Raspberry_Pi_1.GPIO12, J1.GPIO_12
  N38: Raspberry_Pi_1.ID_SC, J1.ID_SC
  N39: Raspberry_Pi_1.GPIO7, J1.GPIO_7
  N40: Raspberry_Pi_1.GPIO8, J1.GPIO_8
  N41: Raspberry_Pi_1.GPIO25, J1.GPIO_25
  N42: Raspberry_Pi_1.GPIO24, J1.GPIO_24
  N43: Raspberry_Pi_1.GPIO23, J1.GPIO_23
  N44: Raspberry_Pi_1.GPIO18, J1.GPIO_18
  N45: Raspberry_Pi_1.GPIO15, J1.GPIO_15
  N46: Raspberry_Pi_1.GPIO14, J1.GPIO_14
  5V: Raspberry_Pi_1.5V, J1.5V

notes:
  OUT3 - orange
  OUT4 - black
  OUT1 - yellow
  OUT2 - brown
  wire 5 - unused (RED)
  M35SP-7
  MITSUMI
  +12V
  GND

custom parts:
  T Cobbler Plus: The T-Cobbler Plus is an add on prototyping board from Adafruit specifically designed for the Raspberry Pi B+ that can break out all those tasty power, GPIO, I2C and SPI pins from the 40-pin header onto a solderless breadboard. This set will make "cobbling together" prototypes with the Pi super easy. The T-Cobbler Plus can plug into any solderless breadboard.
  28BYJ-48 Stepper Motor: 28BYJ-48 gear-reduction stepper motor (small)
